# Fritzing sketch bitSynth (saved by Fritzing 0.9.3b)
breadboards: 4

parts:
  Part1 = Arduino Nano (Rev3.0)
  U5 = 74HC4051 [package=so16]
  U6 = POT [part_number=OSC package=alps_pot]
  U7 = POT [part_number=SPE package=alps_pot]
  U8 = POT [part_number=LEN package=alps_pot]
  U9 = POT [part_number=MOD package=alps_pot]
  U10 = POT [package=alps_pot]
  U11 = POT [package=alps_pot]
  U12 = POT [package=alps_pot]
  U13 = POT [package=alps_pot]
  U14 = POT [package=alps_pot]
  U15 = POT [package=alps_pot]
  U16 = POT [package=alps_pot]
  U17 = POT [package=alps_pot]
  U18 = 74HC4051 [package=so16]
  U19 = 74HC4051 [part_number=MENU package=so16]
  LCD1 = LCD screen
  U20 = 74HC4051 [package=so16]
  S1 = Momentary Switch [package=ksa_sealed_tac_switch]
  S2 = Momentary Switch [package=ksa_sealed_tac_switch]
  S3 = Momentary Switch [package=ksa_sealed_tac_switch]
  S4 = Momentary Switch [package=ksa_sealed_tac_switch]
  S5 = Momentary Switch [package=ksa_sealed_tac_switch]
  S6 = Momentary Switch [package=ksa_sealed_tac_switch]
  S7 = Momentary Switch [package=ksa_sealed_tac_switch]
  S8 = Momentary Switch [package=ksa_sealed_tac_switch]
  S9 = Momentary Switch [package=ksa_sealed_tac_switch]
  R1 = Resistor [tolerance=±5% resistance=220 package="1206 [SMD]"]
  U21 = POT [part_number=LCD package=alps_pot]
  R2 = Resistor [tolerance=±5% resistance=10k package=THT]
  R3 = Resistor [tolerance=±5% resistance=10k package=THT]
  R4 = Resistor [tolerance=±5% resistance=10k package=THT]
  R5 = Resistor [tolerance=±5% resistance=10k package=THT]
  R6 = Resistor [tolerance=±5% resistance=10k package=THT]
  R7 = Resistor [tolerance=±5% resistance=10k package=THT]
  R8 = Resistor [tolerance=±5% resistance=10k package=THT]
  R9 = Resistor [tolerance=±5% resistance=10k package=THT]
  R10 = Resistor [tolerance=±5% resistance=10k package=THT]

nets (from the schematic view):
  GND: Part1.GND, U5.INH, U5.VEE, U5.VSS, U6.E, U7.E, U8.E, U9.E, U10.E, U11.E, U12.E, U13.E, U14.E, U15.E, U16.E, U17.E, U18.INH, U18.VEE, U18.VSS, U19.INH, U19.VEE, U19.VSS, LCD1.VSS, LCD1.R/W, LCD1.LED-, U20.INH, U20.VEE, U20.VSS, S1.2, S2.2, S3.2, S4.2, S5.2, S6.2, S7.2, S8.2, S9.2, U21.E
  N1: Part1.D2, LCD1.RS
  N2: Part1.D3, LCD1.E
  N3: Part1.D4, LCD1.DB7
  N4: Part1.D5, LCD1.DB6
  N5: Part1.D6, LCD1.DB5
  N6: Part1.D7, LCD1.DB4
  N7: Part1.D8, U5.A, U18.A, U19.A, U20.A
  N8: Part1.D9, U5.B, U18.B, U19.B, U20.B
  N9: Part1.D10, U5.C, U18.C, U19.C, U20.C
  N10: Part1.A3, U5.IO
  N11: Part1.A2, U18.IO
  N12: Part1.A1, U20.IO
  N13: Part1.A0, U19.IO
  N14: U5.IO0, S9.4
  N15: U5.VDD, R10.Pin_0
  N16: U6.S, U19.IO0
  5V: U6.A, U7.A, U8.A, U9.A, U10.A, U11.A, U12.A, U13.A, U14.A, U15.A, U16.A, U17.A, U18.VDD, U19.VDD, LCD1.VDD, U20.VDD, R1.Pin_1, U21.A, R2.Pin_0, R3.Pin_0, R4.Pin_0, R5.Pin_0, R6.Pin_0, R7.Pin_0, R8.Pin_0, R9.Pin_0
  N17: U7.S, U19.IO1
  N18: U8.S, U19.IO2
  N19: U9.S, U19.IO3
  N20: U10.S, U18.IO0
  N21: U11.S, U18.IO1
  N22: U12.S, U18.IO2
  N23: U13.S, U18.IO3
  N24: U14.S, U18.IO4
  N25: U15.S, U18.IO5
  N26: U16.S, U18.IO6
  N27: U17.S, U18.IO7
  N28: LCD1.V0, U21.S
  N29: LCD1.LED+, R1.Pin_0
  N30: U20.IO4, S5.3, R6.Pin_1
  N31: U20.IO6, S7.3, R8.Pin_1
  N32: U20.IO7, S8.3, R9.Pin_1
  N33: U20.IO5, S6.3, R7.Pin_1
  N34: U20.IO3, S4.4
  N35: U20.IO0, S1.4
  N36: U20.IO1, S2.4
  N37: U20.IO2, S3.4
  N38: S1.3, R2.Pin_1
  N39: S2.3, R3.Pin_1
  N40: S3.3, R4.Pin_1
  N41: S4.3, R5.Pin_1
  N42: S9.3, R10.Pin_1
